# Fritzing sketch Ampel 0.0.1 (saved by Fritzing 0.8.3b)
breadboards: 1

parts:
  Bauteil1 = Arduino Uno (Rev3)
  LED1 = LED - 5mm [color="Red (633nm)" package="5 mm [THT]"]
  R1 = Resistor [tolerance=±5% resistance=220 package=THT]
  R2 = Resistor [tolerance=±5% resistance=220 package=THT]
  R3 = Resistor [tolerance=±5% resistance=220 package=THT]
  R4 = Resistor [tolerance=±5% resistance=220 package=THT]
  R5 = Resistor [tolerance=±5% resistance=220 package=THT]
  LED2 = LED - 5mm [color="Yellow (595nm)" package="5 mm [THT]"]
  LED3 = LED - 5mm [color="Green (570nm)" package="5 mm [THT]"]
  LED4 = LED - 5mm [color="Red (633nm)" package="5 mm [THT]"]
  LED5 = LED - 5mm [color="Green (565nm)" package="5 mm [THT]"]
  S1 = Pushbutton [package=THT]
  R6 = Resistor [tolerance=±5% resistance=220 package=THT]

nets:
  N1: Bauteil1.GND, LED1.anode, LED2.anode, LED3.anode, LED4.anode, LED5.anode, R6.Pin_1
  N2: Bauteil1.D8, S1.leg0, R6.Pin_0
  N3: Bauteil1.D0/RX, R1.Pin_0
  N4: Bauteil1.D1/TX, R2.Pin_0
  N5: Bauteil1.D2, R3.Pin_0
  N6: Bauteil1.D3_PWM, R4.Pin_0
  N7: Bauteil1.D4, R5.Pin_0
  N8: Bauteil1.5V, S1.leg1
  N9: LED1.cathode, R5.Pin_1
  N10: R1.Pin_1, LED5.cathode
  N11: R2.Pin_1, LED4.cathode
  N12: R3.Pin_1, LED3.cathode
  N13: R4.Pin_1, LED2.cathode
